# Fritzing sketch master_fritzing (saved by Fritzing 0.9.3b)
breadboards: 2

parts:
  Arduino_Uno_2 = Arduino Uno (Rev3) - ICSP
  HC-SR04_front2 = HC-SR04 Ultrasonic Distance Sensor
  HC-SR04_right2 = HC-SR04 Ultrasonic Distance Sensor
  HC-SR04_left2 = HC-SR04 Ultrasonic Distance Sensor
  Battery_9V_2 = Battery block 9V
  Hc_o5_bluetooth_master1 = Bluetooth HC-05 Macho  # not connected
  R3 = Resistor [tolerance=±5% resistance=2.2 package="1206 [SMD]"]
  R4 = Resistor [tolerance=±5% resistance=1 package="1206 [SMD]"]

nets:
  N1: Arduino_Uno_2.A0, HC-SR04_left2.ECHO
  N2: Arduino_Uno_2.A1, HC-SR04_left2.TRIG
  N3: Arduino_Uno_2.A2, HC-SR04_right2.ECHO
  N4: Arduino_Uno_2.A3, HC-SR04_right2.TRIG
  N5: Arduino_Uno_2.A4/SDA, HC-SR04_front2.ECHO
  N6: Arduino_Uno_2.A5/SCL, HC-SR04_front2.TRIG
  N7: Arduino_Uno_2.D1/TX, R3.Pin_0
  VCC: Arduino_Uno_2.5V, HC-SR04_front2.VCC, HC-SR04_right2.VCC, HC-SR04_left2.VCC
  GND: Arduino_Uno_2.GND, HC-SR04_front2.GND, HC-SR04_right2.GND, HC-SR04_left2.GND, Battery_9V_2.-, R4.Pin_0
  N8: R3.Pin_1, R4.Pin_1
