# Fritzing sketch slave_fritzing (saved by Fritzing 0.9.3b)
breadboards: 1

parts:
  Arduino_Uno = Arduino Uno (Rev3) - ICSP
  HC_05_slave_mode = Bluetooth HC-05 Macho  # not connected
  R2 = Resistor [tolerance=±5% resistance=2.2 package="1206 [SMD]"]
  R1 = Resistor [tolerance=±5% resistance=1 package="1206 [SMD]"]

nets:
  N1: Arduino_Uno.D1/TX, R2.Pin_0
  N2: Arduino_Uno.GND, R1.Pin_1
  N3: R2.Pin_1, R1.Pin_0
